# Fritzing sketch TrickleSwitchShield (saved by Fritzing 0.9.3b)
circuit board: 6.88566cm x 5.36311cm
breadboards: 1

parts:
  R8 = Resistor [tolerance=±5% resistance=3.3k package=THT]
  R6 = Resistor [tolerance=±5% resistance=3.3k package=THT]
  R5 = Resistor [tolerance=±5% resistance=3.3k package=THT]
  R1 = Resistor [tolerance=±5% resistance=3.3k package=THT]
  R2 = Resistor [tolerance=±5% resistance=3.3k package=THT]
  R3 = Resistor [tolerance=±5% resistance=3.3k package=THT]
  R4 = Resistor [tolerance=±5% resistance=3.3k package=THT]
  R12 = Resistor [tolerance=±5% resistance=220 package=THT]
  R11 = Resistor [tolerance=±5% resistance=220 package=THT]
  R10 = Resistor [tolerance=±5% resistance=220 package=THT]
  R9 = Resistor [tolerance=±5% resistance=220 package=THT]
  R7 = Resistor [tolerance=±5% resistance=3.3k package=THT]
  J1 = female pin header, 16 pins [form="♀ (female)"]
  J3 = female pin header, 6 pins [form="♀ (female)"]
  D2 = Rectifier Diode [part_number=1N4001 package="300 mil [THT]"]
  D4 = Rectifier Diode [part_number=1N4001 package="300 mil [THT]"]
  D1 = Rectifier Diode [part_number=1N4001 package="300 mil [THT]"]
  D3 = Rectifier Diode [part_number=1N4001 package="300 mil [THT]"]
  C1 = Capacitor [package=cap-pth-small2]
  J4 = female pin header, 1 pin [form="♀ (female)"]
  J6 = female pin header, 1 pin [form="♀ (female)"]
  J7 = female pin header, 1 pin [form="♀ (female)"]
  J8 = female pin header, 1 pin [form="♀ (female)"]
  Part1 = Arduino Uno (Rev3)
  D5 = Rectifier Diode [part_number=1N4001 package="300 mil [THT]"]
  J2 = male pin header, 6 pins [form="♂ (male)"]
  J4_2 = screw terminal, 4 pins

nets:
  N1: R8.Pin_0, J1.pin1, Part1.D13/SCK
  N2: R8.Pin_1, R6.Pin_1, R5.Pin_1, R1.Pin_1, R2.Pin_1, R3.Pin_1, R4.Pin_1, R12.Pin_0, R11.Pin_0, R10.Pin_0, R9.Pin_0, R7.Pin_1, J8.pin1, Part1.GND, J2.pin4
  N3: R6.Pin_0, J1.pin5, Part1.D11_PWM/MOSI
  N4: R5.Pin_0, J1.pin7, Part1.D10_PWM/SS
  N5: R1.Pin_0, J1.pin15
  N6: R2.Pin_0, J1.pin13
  N7: R3.Pin_0, J1.pin11
  N8: R4.Pin_0, J1.pin9
  N9: R12.Pin_1, J3.pin1, Part1.D5_PWM
  N10: R11.Pin_1, J3.pin2, Part1.D4
  N11: R10.Pin_1, J3.pin3, Part1.D3_PWM
  N12: R9.Pin_1, J3.pin4, Part1.D2
  N13: R7.Pin_0, J1.pin3, Part1.D12/MISO
  N14: J1.pin2, J1.pin4, J1.pin6, J1.pin8, J3.pin5, J3.pin6, Part1.5V
  N15: J1.pin10, Part1.D9_PWM
  N16: J1.pin12, Part1.D8
  N17: J1.pin14, Part1.D7
  N18: J1.pin16, Part1.D6_PWM
  N19: D2.cathode, D1.cathode, C1.1, J2.pin2
  N20: D2.anode, D4.cathode, J4_2.pin1, J4_2.pin2
  N21: D4.anode, D3.anode, C1.2, J2.pin5
  N22: D1.anode, D3.cathode, J4_2.pin3, J4_2.pin4
  N23: J4.pin1, J2.pin6
  N24: J6.pin1, J2.pin3
  N25: J7.pin1, D5.anode
  N26: Part1.VIN, D5.cathode, J2.pin1

notes:
  +VAC
  -VAC
  Trickle Switch
  Rev. A
  M. Buffa
  DSN-MINI-360
